# Fritzing sketch Untitled Sketch 3 (saved by Fritzing 0.9.0b)
breadboards: 4

parts:
  Part1 = Arduino Mega ADK (Rev3)
  LED1 = smd LED [color="Red (633nm)" package="0805 [SMD]"]
  LED2 = smd LED [color="Green (570nm)" package="0805 [SMD]"]
  LED3 = smd LED [color="White (4500K)" package="0805 [SMD]"]
  LED4 = smd LED [color="White (4500K)" package="0805 [SMD]"]
  LED5 = smd LED [color="Red (633nm)" package="0805 [SMD]"]
  LED6 = smd LED [color="Red (633nm)" package="0805 [SMD]"]
  LED7 = smd LED [color="Red (633nm)" package="0805 [SMD]"]
  LED8 = smd LED [color="Green (570nm)" package="0805 [SMD]"]
  LED9 = smd LED [color="Green (570nm)" package="0805 [SMD]"]
  LED10 = smd LED [color="Green (570nm)" package="0805 [SMD]"]
  R1 = Resistor [tolerance=±5% resistance=220 package=THT]
  R2 = Resistor [tolerance=±5% resistance=220 package=THT]
  R3 = Resistor [tolerance=±5% resistance=220 package=THT]
  R4 = Resistor [tolerance=±5% resistance=220 package=THT]
  R5 = Resistor [tolerance=±5% resistance=220 package=THT]
  R6 = Resistor [tolerance=±5% resistance=220 package=THT]
  U1 = GAS_SENSOR [package=mq-3]
  R7 = Resistor [tolerance=±5% resistance=100k package="1206 [SMD]"]
  R8 = Photocell (LDR) [package=THT]
  R9 = Photocell (LDR) [package=THT]
  R10 = Photocell (LDR) [package=THT]
  R11 = Resistor [tolerance=±5% resistance=10k package="1206 [SMD]"]
  R12 = Resistor [tolerance=±5% resistance=10k package="1206 [SMD]"]
  R13 = Resistor [tolerance=±5% resistance=10k package="1206 [SMD]"]
  S1 = Toggle Switch [package=THT]
  S2 = Toggle Switch [package=THT]
  S3 = Toggle Switch [package=THT]
  S4 = Toggle Switch [package=THT]
  IC1 = ULN2003A [package="SO16 [SMD]"]
  IC2 = ULN2003A [package="SO16 [SMD]"]
  IC3 = ULN2003A [package="SO16 [SMD]"]
  M2 = Stepper Motor - Unipolar
  M3 = Stepper Motor - Unipolar
  Power_plug1 = Power plug
  M1 = Stepper Motor - Unipolar
  S5 = Pushbutton [package="[THT]"]
  S6 = Pushbutton [package="[THT]"]
  S7 = Pushbutton [package="[THT]"]
  S8 = Pushbutton [package="[THT]"]
  S9 = Toggle Switch [package=THT]
  JP1 = Header 3 [package=screwterminal-3.5mm-3_lock.007s]

nets:
  N1: Part1.A0, U1.B1, R7.Pin_0
  N2: Part1.A1, R10.pin_0, R11.Pin_1
  N3: Part1.A2, R9.pin_0, R12.Pin_1
  N4: Part1.A3, R8.pin_0, R13.Pin_1
  N5: Part1.D18/TX1, S8.Pin_3, S8.Pin_4
  N6: Part1.D17/RX2, S7.Pin_3, S7.Pin_4
  N7: Part1.D16/TX2, S6.Pin_3, S6.Pin_4
  N8: Part1.D15/RX3, S5.Pin_3, S5.Pin_4
  N9: Part1.D14/TX3, S9.L1
  N10: Part1.GND, LED1.anode, LED2.anode, LED3.anode, LED4.anode, LED5.anode, LED6.anode, LED7.anode, LED8.anode, LED9.anode, LED10.anode, R8.pin_1, R9.pin_1, R10.pin_1, S1.L1, S2.L1, S3.L1, S4.L1, S5.Pin_1, S5.Pin_2, S6.Pin_1, S6.Pin_2, S7.Pin_1, S7.Pin_2, S8.Pin_1, S8.Pin_2, S9.COM, JP1.2
  N11: Part1.D10_PWM, R5.Pin_1
  N12: Part1.D9_PWM, R6.Pin_1
  N13: Part1.D8_PWM, JP1.3
  N14: Part1.5V, U1.A1, U1.H1, U1.H2, R7.Pin_1, R11.Pin_0, R12.Pin_0, R13.Pin_0, JP1.1
  N15: Part1.D2_PWM, S1.COM
  N16: Part1.D3_PWM, S2.COM
  N17: Part1.D4_PWM, S3.COM
  N18: Part1.D5_PWM, S4.COM
  N19: Part1.D6_PWM, R3.Pin_1, R4.Pin_1
  N20: Part1.D7_PWM, R2.Pin_1
  N21: Part1.D22, IC1.In_1
  N22: Part1.D24, IC1.In_2
  N23: Part1.D26, IC1.In_3
  N24: Part1.D28, IC1.In_4
  N25: Part1.D46, IC3.In_1
  N26: Part1.D47, IC2.In_1
  N27: Part1.D48, IC3.In_2
  N28: Part1.D49, IC2.In_2
  N29: Part1.D50/MISO, IC3.In_3
  N30: Part1.D51/MOSI, IC2.In_3
  N31: Part1.D52/SCK, IC3.In_4
  N32: Part1.D53/SS, IC2.In_4
  N33: LED1.cathode, LED5.cathode, R1.Pin_0
  N34: LED2.cathode, LED8.cathode, R3.Pin_0
  N35: LED3.cathode, R5.Pin_0
  N36: LED4.cathode, R6.Pin_0
  N37: LED6.cathode, LED7.cathode, R2.Pin_0
  N38: LED9.cathode, LED10.cathode, R4.Pin_0
  N39: IC1.0V, IC2.0V, IC3.0V, Power_plug1.GND
  N40: IC1.COM_-_Common, IC2.COM_-_Common, IC3.COM_-_Common, M2.COMMON_1, M2.COMMON_2, M3.COMMON_1, M3.COMMON_2, Power_plug1.VCC, M1.COMMON_1, M1.COMMON_2
  N41: IC1.Out_4, M1.D
  N42: IC1.Out_3, M1.B
  N43: IC1.Out_2, M1.C
  N44: IC1.Out_1, M1.A
  N45: IC2.Out_4, M2.D
  N46: IC2.Out_3, M2.B
  N47: IC2.Out_2, M2.C
  N48: IC2.Out_1, M2.A
  N49: IC3.Out_4, M3.D
  N50: IC3.Out_3, M3.B
  N51: IC3.Out_2, M3.C
  N52: IC3.Out_1, M3.A
