# Fritzing sketch schematic (saved by Fritzing 0.9.0b)
breadboards: 2

parts:
  Part1 = Arduino Mega ADK (Rev3)
  Part2 = SRF05 Ultrasonic Rangefinder
  Part3 = SRF05 Ultrasonic Rangefinder
  Part4 = SRF05 Ultrasonic Rangefinder
  M1 = Stepper Motor - Unipolar
  M2 = Stepper Motor - Unipolar
  M3 = Stepper Motor - Unipolar
  IC1 = ULN2003A [package="SO16 [SMD]"]
  IC2 = ULN2003A [package="SO16 [SMD]"]
  IC3 = ULN2003A [package="SO16 [SMD]"]

nets:
  N1: Part1.D12_PWM, Part2.Trig
  N2: Part1.D11_PWM, Part2.Echo
  N3: Part1.D10_PWM, Part3.Trig
  N4: Part1.D9_PWM, Part3.Echo
  N5: Part1.D8_PWM, Part4.Trig
  VCC: Part1.5V, Part2.VCC, Part3.VCC, Part4.VCC, IC1.COM_-_Common, IC2.COM_-_Common, IC3.COM_-_Common
  GND: Part1.GND, Part2.GND, Part3.GND, Part4.GND, IC1.0V, IC2.0V, IC3.0V
  N6: Part1.D6_PWM, Part4.Echo
  N7: Part1.D22, IC1.In_1
  N8: Part1.D24, IC1.In_2
  N9: Part1.D26, IC1.In_3
  N10: Part1.D28, IC1.In_4
  N11: Part1.D30, IC2.In_1
  N12: Part1.D32, IC2.In_2
  N13: Part1.D34, IC2.In_3
  N14: Part1.D36, IC2.In_4
  N15: Part1.D38, IC3.In_1
  N16: Part1.D40, IC3.In_2
  N17: Part1.D42, IC3.In_3
  N18: Part1.D44, IC3.In_4
  N19: M1.A, IC1.Out_1
  N20: M1.C, IC1.Out_2
  N21: M1.B, IC1.Out_3
  N22: M1.D, IC1.Out_4
  N23: M2.A, IC2.Out_1
  N24: M2.C, IC2.Out_2
  N25: M2.B, IC2.Out_3
  N26: M2.D, IC2.Out_4
  N27: M3.A, IC3.Out_1
  N28: M3.C, IC3.Out_2
  N29: M3.B, IC3.Out_3
  N30: M3.D, IC3.Out_4
