# Fritzing sketch Untitled Sketch (saved by Fritzing 0.9.0b)
breadboards: 3

parts:
  U2 = LCD-16X2 [package=lcd-16x2]
  Part1 = Arduino Mega ADK (Rev3)
  Matrix_keypad1 = KEYPAD 4x4
  Q1 = LTR-301 [package=ltr-301]
  D1 = LTE-302 [package=lte-302]
  R1 = Resistor [tolerance=±5% resistance=100 package="0603 [SMD]"]
  R2 = Resistor [tolerance=±5% resistance=10k package="1206 [SMD]"]
  LED1 = LEDs [package=led10mm]
  LED2 = LEDs [package=led10mm]
  LED3 = LEDs [package=led10mm]
  LED4 = LEDs [package=led10mm]
  S1 = SWITCH-MOMENTARY-2 [package=tactile-switch-1101ne]
  IC1 = ULN2003A [package="SO16 [SMD]"]
  IC2 = ULN2003A [package="SO16 [SMD]"]
  IC3 = ULN2003A [package="SO16 [SMD]"]
  VCC1 = Battery block 9V
  M1 = Stepper Motor - Unipolar
  M2 = Stepper Motor - Unipolar
  M3 = Stepper Motor - Unipolar

nets:
  VSS: U2.VSS, U2.R_W, U2.K, Part1.GND, Q1.C, D1.C, LED1.C, LED2.C, LED3.C, LED4.C, S1.2
  VDD: U2.VDD, U2.A, Part1.5V, R1.Pin_1, R2.Pin_0
  N1: U2.VO, Part1.D12_PWM
  N2: U2.RS, Part1.D52/SCK
  N3: U2.E, Part1.D50/MISO
  N4: U2.DB4, Part1.D48
  N5: U2.DB5, Part1.D46
  N6: U2.DB6, Part1.D44
  N7: U2.DB7, Part1.D42
  N8: Part1.A0, D1.A, R1.Pin_0
  N9: Part1.D18/TX1, S1.1
  N10: Part1.D8_PWM, LED4.A
  N11: Part1.D3_PWM, LED1.A
  N12: Part1.D4_PWM, LED2.A
  N13: Part1.D5_PWM, LED3.A
  N14: Part1.D24, Matrix_keypad1.row4
  N15: Part1.D26, Matrix_keypad1.row3
  N16: Part1.D28, Matrix_keypad1.row2
  N17: Part1.D30, Matrix_keypad1.row1
  N18: Part1.D31, IC2.In_1
  N19: Part1.D32, Matrix_keypad1.col4
  N20: Part1.D33, IC2.In_2
  N21: Part1.D34, Matrix_keypad1.col3
  N22: Part1.D35, IC2.In_3
  N23: Part1.D36, Matrix_keypad1.col2
  N24: Part1.D37, IC2.In_4
  N25: Part1.D38, Matrix_keypad1.col1
  N26: Part1.D39, IC1.In_1
  N27: Part1.D41, IC1.In_2
  N28: Part1.D43, IC1.In_3
  N29: Part1.D45, IC1.In_4
  N30: Part1.D47, IC3.In_1
  N31: Part1.D49, IC3.In_2
  N32: Part1.D51/MOSI, IC3.In_3
  N33: Part1.D53/SS, IC3.In_4
  N34: Q1.E, R2.Pin_1
  N35: IC1.0V, IC2.0V, IC3.0V, VCC1.-
  N36: IC1.COM_-_Common, IC2.COM_-_Common, IC3.COM_-_Common, VCC1.+, M1.COMMON_1, M1.COMMON_2, M2.COMMON_1, M2.COMMON_2, M3.COMMON_1, M3.COMMON_2
  N37: IC1.Out_4, M2.D
  N38: IC1.Out_3, M2.B
  N39: IC1.Out_2, M2.C
  N40: IC1.Out_1, M2.A
  N41: IC2.Out_4, M1.D
  N42: IC2.Out_3, M1.B
  N43: IC2.Out_2, M1.C
  N44: IC2.Out_1, M1.A
  N45: IC3.Out_4, M3.D
  N46: IC3.Out_3, M3.B
  N47: IC3.Out_2, M3.C
  N48: IC3.Out_1, M3.A

custom parts:
  KEYPAD 4x4: Matrix keypad 16 buttons, 4 rows x 4 columns
